# Fritzing sketch pcb-lcd (saved by Fritzing 0.9.3b)
circuit board: 6cm x 4.5cm
breadboards: 1

parts:
  Part3 = Bluetooth HC-05 Macho
  Arduino_Nano_1 = Arduino Nano (Rev3.0)
  Finger_print2 = Bluetooth HC-05 Macho
  part = Bluetooth HC-05 Macho
  Power = Toggle Switch [package=THT]

nets:
  N1: Part3.TXD, Arduino_Nano_1.D0/RX
  N2: Part3.RXD, Arduino_Nano_1.D1/TX
  VCC: Part3.VCC, Arduino_Nano_1.5V, Finger_print2.VCC, part.VCC, Power.L2
  GND: Part3.GND, Arduino_Nano_1.GND, Finger_print2.GND, part.GND, Power.L1
  N3: Arduino_Nano_1.D2, Finger_print2.TXD
  N4: Arduino_Nano_1.D3, Finger_print2.RXD
  N5: Arduino_Nano_1.A5, part.TXD
  N6: Arduino_Nano_1.A4, part.RXD

notes:
  Smart Medical System
  +
  -
  version 2.0.0
  SDA
  SCL
  GND
  5V
  P2
  P1
  RX
  TX
